# Fritzing sketch NodeMCU_test (saved by Fritzing 0.9.2b)
circuit board: 3.91508cm x 5.48866cm
breadboards: 1

parts:
  J2 = female pin header, 4 pins [form="♀ (female)"]
  74HC164 = IC, DIP package, 16 pins [chip_label=74HC164]
  U2 = 74HC595 [package="DIP16 [THT]"]
  J3 = female pin header, 4 pins [form="♀ (female)"]
  J1 = female pin header, 4 pins [form="♀ (female)"]
  U1 = NodeMCU V1.0
  J4 = female pin header, 4 pins [form="♀ (female)"]
  J6 = female pin header, 8 pins [form="♀ (female)"]
  J7 = female pin header, 8 pins [form="♀ (female)"]

nets:
  N1: J2.pin1, 74HC164.pin16, U2.MR, U2.VCC, J3.pin1, J1.pin1, J4.pin1
  N2: J2.pin2, U2.OE, J3.pin2, J1.pin2, J4.pin2
  N3: J2.pin3, J3.pin3, J1.pin3, U1.D2, J4.pin3
  N4: J2.pin4, J3.pin4, J1.pin4, U1.D1, J4.pin4
  N5: 74HC164.pin1, U1.D3
  N6: 74HC164.pin2, U1.D5
  N7: 74HC164.pin3, J6.pin5
  N8: 74HC164.pin4, J6.pin6
  N9: 74HC164.pin5, J6.pin7
  N10: 74HC164.pin6, J6.pin8
  GND: 74HC164.pin8, U2.GND, U1.GND
  N11: 74HC164.pin9, U1.SD3
  N12: 74HC164.pin11, J6.pin1
  N13: 74HC164.pin12, J6.pin2
  N14: 74HC164.pin13, J6.pin3
  N15: 74HC164.pin14, J6.pin4
  N16: 74HC164.pin15, U1.D4
  N17: U2.Q1, J7.pin2
  N18: U2.Q2, J7.pin3
  N19: U2.Q3, J7.pin4
  N20: U2.Q4, J7.pin5
  N21: U2.Q5, J7.pin6
  N22: U2.Q6, J7.pin7
  N23: U2.Q7, J7.pin8
  N24: U2.SH_CP, U1.D6
  N25: U2.ST_CP, U1.D7
  N26: U2.DS, U1.D8
  N27: U2.Q0, J7.pin1

notes:
  I2C
  INPUT
  OUTPUT

custom parts:
  NodeMCU V1.0: ESP9266 based NodeMCU
