# Fritzing sketch Leaflift_core_v1.1 (saved by Fritzing 0.9.3b)
circuit board: 9.61714cm x 5.33114cm
breadboards: 4

parts:
  C1 = Electrolytic Capacitor [capacitance=47µF voltage=16V package="100 mil [THT, electrolytic]"]
  C2 = Ceramic Capacitor [capacitance=10µF voltage=16V package="100 mil [THT, multilayer]"]  # not connected
  C3 = Electrolytic Capacitor [capacitance=47µF voltage=16V package="100 mil [THT, electrolytic]"]  # not connected
  JP1 = Header 8 [package=bm08b-srss-tb]  # not connected
  JP2 = Header 4 [package=1x04-1mm-ra]  # not connected
  pH_Circuit = pH Circuit
  Probe_BNC = Pre-Assembled Female BNC
  RHT1 = Humidity and Temperature Sensor RHT03  # not connected
  S1 = Pushbutton [package="[THT]"]  # not connected
  S2 = Toggle Switch [package=THT]  # not connected
  U6 = Voltage Regulator - 5V [package="TO220 [THT]"]  # not connected
  3 = female pin header, 4 pins [form="♀ (female)"]
  bmp = female pin header, 4 pins [form="♀ (female)"]
  lux = female pin header, 4 pins [form="♀ (female)"]
  SCL = Pad [width=1.5051851851851958 height=19.379259259259253 connect=center]  # not connected
  SDA = Pad [width=1.9755555555555555 height=22.107407407407408 connect=center]  # not connected
  10k = Resistor [tolerance=±5% resistance=10k package=THT]
  sx3 = female pin header, 12 pins [form="♀ (female)"]
  sx4 = female pin header, 12 pins [form="♀ (female)"]
  MCP23017 = IC, DIP package, 28 pins [chip_label=MCP23017]
  3_2 = female pin header, 4 pins [form="♀ (female)"]
  A0 = female pin header, 3 pins [form="♀ (female)"]  # not connected
  UART = female pin header, 4 pins [form="♀ (female)"]  # not connected
  FTDI = female pin header, 6 pins [form="♀ (female)"]  # not connected
  U4 = RJ45 Jack [package=rj45-8]  # not connected
  U2 = RJ45 Jack [package=rj45-8]  # not connected
  U3 = RJ45 Jack [package=rj45-8]  # not connected
  U7 = RJ45 Jack [package=rj45-8]  # not connected
  U5 = RJ45 Jack [package=rj45-8]  # not connected

nets:
  N1: C1.-, pH_Circuit.GND#0, 3.pin2, bmp.pin2, lux.pin2, sx3.pin6, sx4.pin6, MCP23017.pin10, MCP23017.pin15, MCP23017.pin16, MCP23017.pin17, 3_2.pin2
  N2: C1.+, pH_Circuit.Vcc, Probe_BNC.NC, 3.pin1, bmp.pin1, lux.pin1, 10k.Pin_1, sx3.pin5, sx4.pin5, MCP23017.pin9, 3_2.pin1
  N3: pH_Circuit.TX, 3.pin4, bmp.pin4, lux.pin4, sx3.pin12, sx4.pin12, MCP23017.pin12, 3_2.pin4
  N4: pH_Circuit.RX, 3.pin3, bmp.pin3, lux.pin3, sx3.pin11, sx4.pin11, MCP23017.pin13, 3_2.pin3
  N5: pH_Circuit.PRB, Probe_BNC.PRB
  N6: pH_Circuit.GND#5, Probe_BNC.GND
  N7: 10k.Pin_0, MCP23017.pin18
  N8: sx3.pin1, MCP23017.pin21
  N9: sx3.pin2, MCP23017.pin22
  N10: sx3.pin3, MCP23017.pin23
  N11: sx3.pin4, MCP23017.pin24
  N12: sx3.pin7, MCP23017.pin25
  N13: sx3.pin8, MCP23017.pin26
  N14: sx3.pin9, MCP23017.pin27
  N15: sx3.pin10, MCP23017.pin28
  N16: sx4.pin1, MCP23017.pin8
  N17: sx4.pin2, MCP23017.pin7
  N18: sx4.pin3, MCP23017.pin6
  N19: sx4.pin4, MCP23017.pin5
  N20: sx4.pin7, MCP23017.pin4
  N21: sx4.pin8, MCP23017.pin3
  N22: sx4.pin9, MCP23017.pin2
  N23: sx4.pin10, MCP23017.pin1

notes:
  leaflift v1.0
  SDA | SCL
  SDA
  SCL
  1W
  3V
  GND
