# Fritzing sketch Leaflift_core_v1 (saved by Fritzing 0.9.3b)
circuit board: 9.33227cm x 2.55498cm
circuit board: 6.52884cm x 5.26901cm
circuit board: 8.11871cm x 5.06676cm
breadboards: 3

parts:
  C1 = Electrolytic Capacitor [capacitance=47µF voltage=16V package="100 mil [THT, electrolytic]"]
  U1 = NodeMCU V1.0
  320x160_LCD = OLED 0.96" 128x64 I2C SSD1306  # not connected
  C2 = Ceramic Capacitor [capacitance=10µF voltage=16V package="100 mil [THT, multilayer]"]
  C3 = Electrolytic Capacitor [capacitance=47µF voltage=16V package="100 mil [THT, electrolytic]"]  # not connected
  U2 = RJ45 Jack [package=rj45-8]  # not connected
  JP1 = Header 8 [package=bm08b-srss-tb]  # not connected
  JP2 = Header 4 [package=1x04-1mm-ra]  # not connected
  pH_Circuit1 = pH Circuit
  Female_BNC1 = Pre-Assembled Female BNC
  D4 = Rectifier Diode [part_number=1N4001 package="300 mil [THT]"]
  D5 = Rectifier Diode [part_number=1N4001 package="300 mil [THT]"]
  D6 = Rectifier Diode [part_number=1N4001 package="300 mil [THT]"]
  D7 = Rectifier Diode [part_number=1N4001 package="300 mil [THT]"]
  R1 = Resistor [tolerance=±5% resistance=10k package=THT]
  U3 = RJ45 Jack [package=rj45-8]  # not connected
  U4 = RJ45 Jack [package=rj45-8]  # not connected
  U5 = RJ45 Jack [package=rj45-8]  # not connected
  RHT1 = Humidity and Temperature Sensor RHT03  # not connected
  S1 = Pushbutton [package="[THT]"]  # not connected
  S2 = Toggle Switch [package=THT]  # not connected
  U6 = Voltage Regulator - 5V [package="TO220 [THT]"]  # not connected
  Power_plug1 = Power plug
  J2 = female pin header, 4 pins [form="♀ (female)"]
  U7 = RJ45 Jack [package=rj45-8]  # not connected
  J3 = female pin header, 4 pins [form="♀ (female)"]
  J4 = female pin header, 4 pins [form="♀ (female)"]
  J5 = female pin header, 4 pins [form="♀ (female)"]
  J6 = female pin header, 4 pins [form="♀ (female)"]
  J7 = female pin header, 2 pins [form="♀ (female)"]
  J8 = female pin header, 1 pin [form="♀ (female)"]
  J9 = female pin header, 1 pin [form="♀ (female)"]
  J10 = female pin header, 4 pins [form="♀ (female)"]
  J11 = female pin header, 4 pins [form="♀ (female)"]
  J12 = female pin header, 4 pins [form="♀ (female)"]
  Pad1 = Pad [width=27.375555555555554 height=0.84666666666666657 connect=center]  # not connected
  Pad2 = Pad [width=27.375555555555554 height=0.84666666666666657 connect=center]  # not connected
  J13 = female pin header, 4 pins [form="♀ (female)"]  # not connected
  I2C = IC, DIP package, 28 pins [chip_label=MCP23017]

nets:
  N1: C1.-, U1.GND, C2.0, I2C.pin15, I2C.pin16, I2C.pin17
  N2: C1.+, U1.3V3, R1.Pin_1
  N3: U1.D1, J10.pin4, J11.pin4, J12.pin4, I2C.pin13
  N4: U1.D2, J10.pin3, J11.pin3, J12.pin3, I2C.pin12
  N5: U1.Vin, C2.1
  N6: U1.A0, D4.anode, D5.anode, D6.anode, D7.anode, J8.pin1, J9.pin1
  N7: pH_Circuit1.Vcc, Female_BNC1.NC
  N8: pH_Circuit1.PRB, Female_BNC1.PRB
  N9: pH_Circuit1.GND#5, Female_BNC1.GND
  N10: D4.cathode, J5.pin4
  N11: D5.cathode, J2.pin4
  N12: D6.cathode, J4.pin4
  N13: D7.cathode, J3.pin4
  N14: R1.Pin_0, I2C.pin18
  N15: Power_plug1.GND, J10.pin2, J11.pin2, J12.pin2, I2C.pin10
  N16: Power_plug1.VCC, J10.pin1, J11.pin1, J12.pin1, I2C.pin9
  N17: J2.pin1, J6.pin2
  N18: J2.pin2, J3.pin2, J4.pin2, J5.pin2, J7.pin1
  N19: J3.pin1, J6.pin4
  N20: J4.pin1, J6.pin3
  N21: J5.pin1, J6.pin1

custom parts:
  NodeMCU V1.0: ESP9266 based NodeMCU
