# Fritzing sketch Leaflift_soil_v1 (saved by Fritzing 0.9.3b)
circuit board: 3.03401cm x 2.64905cm
breadboards: 1

parts:
  D2 = Rectifier Diode [part_number=1N4001 package="300 mil [THT]"]
  D3 = Rectifier Diode [part_number=1N4001 package="300 mil [THT]"]
  D4 = Rectifier Diode [part_number=1N4001 package="300 mil [THT]"]
  D1 = Rectifier Diode [part_number=1N4001 package="300 mil [THT]"]
  RHT1 = Humidity and Temperature Sensor RHT03  # not connected
  S1 = Pushbutton [package="[THT]"]  # not connected
  S2 = Toggle Switch [package=THT]  # not connected
  U6 = Voltage Regulator - 5V [package="TO220 [THT]"]  # not connected
  s1 = female pin header, 4 pins [form="♀ (female)"]
  s2 = female pin header, 4 pins [form="♀ (female)"]
  s3 = female pin header, 4 pins [form="♀ (female)"]
  s4 = female pin header, 4 pins [form="♀ (female)" part_number=soil1]
  sx = female pin header, 4 pins [form="♀ (female)"]
  gnd = female pin header, 2 pins [form="♀ (female)"]
  A0 = female pin header, 1 pin [form="♀ (female)"]
  SCL = Pad [width=1.5051851851851958 height=19.379259259259253 connect=center]  # not connected
  SDA = Pad [width=1.9755555555555555 height=22.107407407407408 connect=center]  # not connected
  sx2 = female pin header, 12 pins [form="♀ (female)"]  # not connected
  sx1 = female pin header, 12 pins [form="♀ (female)"]  # not connected

nets:
  N1: D2.cathode, D4.cathode, s2.pin4, s4.pin4
  N2: D2.anode, D3.anode, D4.anode, D1.anode, A0.pin1
  N3: D3.cathode, s3.pin4
  N4: D1.cathode, s1.pin4
  N5: s1.pin1, sx.pin1
  N6: s1.pin2, s2.pin2, s3.pin2, s4.pin2, gnd.pin1, gnd.pin2
  N7: s2.pin1, sx.pin2
  N8: s3.pin1, sx.pin3
  N9: s4.pin1, sx.pin4

notes:
  leaflift v1.0
  SDA
  SCL
  1W
  3V
  GND
